# Fritzing sketch Rain (saved by Fritzing 0.9.3b)

parts:
  YL-83_-_Control_Board = YL-83 Rain Sensor - Control Board
  YL-83_-_Detection_Board1 = YL-83 Rain Sensor - Detection Board
  Pro_Micro = SparkFun Pro Micro
  LED1 = LED - 5mm [color="Red (633nm)" package="5 mm [THT]"]
  S1 = Momentary Switch [package=ksa_sealed_tac_switch]
  S2 = Pushbutton [package="[SMD]"]
  S3 = Momentary Switch [package=ksa_sealed_tac_switch]
  R2 = Resistor [tolerance=±5% resistance=10 package="0805 [SMD]"]
  R3 = Resistor [tolerance=±5% resistance=10 package="0805 [SMD]"]  # not connected
  R4 = Resistor [tolerance=±5% resistance=10 package="0805 [SMD]"]  # not connected
  LED2 = LED - 5mm [color="Red (633nm)" package="5 mm [THT]"]
  LED3 = LED - 5mm [color="Red (633nm)" package="5 mm [THT]"]
  R5 = Resistor [tolerance=±5% resistance=220 package="0805 [SMD]"]
  R6 = Resistor [tolerance=±5% resistance=220 package="0805 [SMD]"]
  R7 = Resistor [tolerance=±5% resistance=220 package="0805 [SMD]"]
  2_Channel_Relay1 = 2 Channel Power Relay

nets:
  VCC: YL-83_-_Control_Board.VCC, Pro_Micro.VCC, S1.4, S2.Pin_3, S2.Pin_4, S3.4, 2_Channel_Relay1.VCC#14
  GND: YL-83_-_Control_Board.GND, Pro_Micro.GND, 2_Channel_Relay1.GND
  N1: YL-83_-_Control_Board.DO, Pro_Micro.2
  N2: YL-83_-_Control_Board.AO, Pro_Micro.A0
  N3: YL-83_-_Control_Board.POS, YL-83_-_Detection_Board1.POS
  N4: YL-83_-_Control_Board.NEG, YL-83_-_Detection_Board1.NEG
  N5: Pro_Micro.5, S2.Pin_1, S2.Pin_2
  N6: Pro_Micro.6, S3.1
  N7: Pro_Micro.7, LED1.anode
  N8: Pro_Micro.8, LED2.anode
  N9: Pro_Micro.9, LED3.anode
  N10: Pro_Micro.15, 2_Channel_Relay1.IN1, 2_Channel_Relay1.IN2
  N11: LED1.cathode, R5.Pin_0
  N12: R2.Pin_1, R7.Pin_1
  N13: LED2.cathode, R6.Pin_0
  N14: LED3.cathode, R7.Pin_0
  N15: 2_Channel_Relay1.JD-VCC, 2_Channel_Relay1.VCC#9

custom parts:
  YL-83 Rain Sensor - Control Board: The YL-83 is a rain sensor that has more resistance when dry and less resistance when wet. The module runs at 5V.
  YL-83 Rain Sensor - Detection Board: The YL-83 is a rain sensor that has more resistance when dry and less resistance when wet. The module runs at 5V.
  SparkFun Pro Micro: The Pro Micro is similar to the Pro Mini except with an ATmega32U4 on board. The USB transceiver inside the 32U4 allows us to add USB connectivity on-board and do away with bulky external USB interface. Based on: https://github.com/unorthodox-engineers/unorthodox-arduino/blob/master/Unorthodox/fritzing/parts/Pro%20Micro.fzpz
  2 Channel Power Relay: A 2 channel power relay. The module operates at 5V.
